# Fritzing sketch arduino-lego-truck-manual-app (saved by Fritzing 0.9.3b)
breadboards: 2

parts:
  Part1 = Arduino Uno (Rev3)
  IC1 = L293D [package=THT]
  Lego_battery_plug_9V_dark_grey_1 = DIP - 8 pins [chip_label=IC package="DIP (Dual Inline) [THT]"]
  Part2 = Bluetooth HC-05 Macho
  R1 = Resistor [tolerance=±5% resistance=1k package=THT]
  R2 = Resistor [tolerance=±5% resistance=1k package=THT]
  R3 = Resistor [tolerance=±5% resistance=1k package=THT]
  Lego_motors_plug_light_grey_2 = DIP - 8 pins [chip_label=IC package="DIP (Dual Inline) [THT]"]
  Lego_servo_plug_light_grey_3 = DIP - 8 pins [chip_label=IC package="DIP (Dual Inline) [THT]"]
  U2 = 74HC595 [package="DIP16 [THT]"]
  LED1 = LED - 3mm [color="Red (633nm)" package="3 mm [THT]"]
  LED2 = LED - 3mm [color="Red (633nm)" package="3 mm [THT]"]
  LED3 = LED - 3mm [color="Red (633nm)" package="3 mm [THT]"]
  LED4 = LED - 3mm [color="White (6500K)" package="3 mm [THT]"]
  LED5 = LED - 3mm [color="White (6500K)" package="3 mm [THT]"]
  LED6 = LED - 3mm [color="Yellow (592nm)" package="3 mm [THT]"]
  LED7 = LED - 3mm [color="Yellow (592nm)" package="3 mm [THT]"]
  LED8 = LED - 3mm [color="Blue (470nm)" package="3 mm [THT]"]
  LED9 = LED - 3mm [color="Blue (470nm)" package="3 mm [THT]"]
  LED10 = LED - 3mm [color="Red (633nm)" package="3 mm [THT]"]
  LED11 = LED - 3mm [color="Yellow (592nm)" package="3 mm [THT]"]
  LED12 = LED - 3mm [color="Yellow (592nm)" package="3 mm [THT]"]
  R7 = Resistor [tolerance=±5% resistance=220 package=THT]
  R8 = Resistor [tolerance=±5% resistance=220 package=THT]
  R9 = Resistor [tolerance=±5% resistance=220 package=THT]
  R10 = Resistor [tolerance=±5% resistance=220 package=THT]
  R11 = Resistor [tolerance=±5% resistance=220 package=THT]
  R12 = Resistor [tolerance=±5% resistance=220 package=THT]
  R13 = Resistor [tolerance=±5% resistance=220 package=THT]
  R14 = Resistor [tolerance=±5% resistance=220 package=THT]

nets:
  N1: Part1.D8, IC1.In_4
  N2: Part1.D9_PWM, IC1.Enable_1
  N3: Part1.D11_PWM/MOSI, U2.DS
  N4: Part1.D12/MISO, U2.ST_CP
  N5: Part1.D13/SCK, U2.SH_CP
  GND: Part1.GND, IC1.0V, Lego_battery_plug_9V_dark_grey_1.GND, Part2.GND, R1.Pin_1, Lego_motors_plug_light_grey_2.GND, Lego_servo_plug_light_grey_3.GND, U2.GND, U2.OE, LED1.anode, LED2.anode, LED4.anode, LED5.anode, LED8.anode, LED9.anode, LED11.anode, LED12.anode
  N6: Part1.D0/RX, Part2.TXD
  N7: Part1.D1/TX, R3.Pin_0
  N8: Part1.D2, IC1.In_1
  N9: Part1.D3_PWM, IC1.Enable_2
  N10: Part1.D5_PWM, IC1.In_2
  N11: Part1.D6_PWM, IC1.In_3
  VCC: Part1.5V, IC1.+V, Part2.VCC, U2.MR, U2.VCC
  N12: IC1.Out_1_(_Controlled_by_Enable_1_), Lego_motors_plug_light_grey_2.C1
  N13: IC1.Out_2_(_Controlled_by_Enable_1_), Lego_motors_plug_light_grey_2.C2
  N14: IC1.+Vmotor, Lego_battery_plug_9V_dark_grey_1.V_lego_(9V), Lego_motors_plug_light_grey_2.V_lego_(9V), Lego_servo_plug_light_grey_3.V_lego_(9V)
  N15: IC1.Out_3_(_Controlled_by_Enable_2_), Lego_servo_plug_light_grey_3.C2
  N16: IC1.Out_4_(_Controlled_by_Enable_2_), Lego_servo_plug_light_grey_3.C1
  N17: Part2.RXD, R2.Pin_0, R3.Pin_1
  N18: R1.Pin_0, R2.Pin_1
  N19: U2.Q1, R7.Pin_1
  N20: U2.Q2, R8.Pin_1
  N21: U2.Q3, R10.Pin_1
  N22: U2.Q4, R11.Pin_1
  N23: U2.Q5, R9.Pin_1
  N24: U2.Q6, R12.Pin_1
  N25: U2.Q7, R13.Pin_1
  N26: U2.Q0, R14.Pin_1
  N27: LED1.cathode, LED3.anode
  N28: LED2.cathode, LED10.anode
  N29: LED3.cathode, R8.Pin_0
  N30: LED4.cathode, R10.Pin_0
  N31: LED5.cathode, R11.Pin_0
  N32: LED6.cathode, R9.Pin_0
  N33: LED6.anode, LED11.cathode
  N34: LED7.cathode, R12.Pin_0
  N35: LED7.anode, LED12.cathode
  N36: LED8.cathode, R13.Pin_0
  N37: LED9.cathode, R14.Pin_0
  N38: LED10.cathode, R7.Pin_0

notes:
  flash light 1
  flash light 2
  turn light left
  turn light right
  head light 1
  head light 2
  tail light
  break light
  5V
  9V
  Disconnect port 1 and 2 when
  uploading code to Arduino

custom parts:
  DIP - 8 pins: A DIP stand-in part for whatever IC you want. With 8 pins on a 300mil dual inline package (DIP) footprint.
